// Logisim project 8b_cpu_isa2.circ as structural Verilog: 1 circuit, main circuit main
module main (
);

  wire decoder_1_out0, decoder_1_out1, decoder_1_out2, decoder_1_out3, Reset_out, SingleStep_out;
  wire [2:0] decoder_1_out9, ProgramROM_data_2;
  wire [4:0] ProgramROM_data;
  wire [7:0] ACC_q, demultiplexer_1_out0, demultiplexer_1_out1, demultiplexer_1_out2, demultiplexer_1_out3,
       demultiplexer_1_out4, demultiplexer_1_out5, demultiplexer_1_out6, demultiplexer_1_out7,
       MainMemoryRAM_dout, multiplexer_1_out, PC_q, rX_q, STAT_q;

  Button SingleStep (.out(SingleStep_out));
  // Probe on ProgramROM_data
  Button Reset (.out(Reset_out));
  Decoder #(.select(5)) decoder_1 (
    .out0(decoder_1_out0), .out1(decoder_1_out1), .out2(decoder_1_out2), .out3(decoder_1_out3),
    .out4(decoder_1_out9[1]), .out5(decoder_1_out9[2]), .out9(decoder_1_out9[0]), .sel(ProgramROM_data),
    .en(SingleStep_out));  // open: out6, out7, out8, out10, out11, out12, out13, out14, out15, out16, out17, out18, out19, out20, out21, out22, out23, out24, out25, out26, out27, out28, out29, out30, out31
  // Probe on ProgramROM_data_2
  // Probe on decoder_1_out1
  ROM ProgramROM (.addr(PC_q), .data({ProgramROM_data, ProgramROM_data_2}));
  // Probe on decoder_1_out2
  // Probe on decoder_1_out3
  // Probe on {{5{1'b0}}, ProgramROM_data_2}
  Register STAT (.Q(STAT_q));  // open: D, en, clk, clr
  // Probe on {ProgramROM_data, ProgramROM_data_2}
  Register ACC (
    .D({{5{1'b0}}, ProgramROM_data_2}), .en(decoder_1_out1), .clk(decoder_1_out1), .Q(ACC_q), .clr(Reset_out));
  Counter #(.trigger("falling")) PC (
    .clr(Reset_out), .up(1'b1), .count(1'b1), .clk(SingleStep_out), .Q(PC_q));  // open: load, D, carry
  // Probe on ACC_q
  Register rX (.D(MainMemoryRAM_dout), .en(decoder_1_out2), .clk(decoder_1_out2), .Q(rX_q), .clr(Reset_out));
  // Probe on multiplexer_1_out
  Multiplexer #(.select(3), .width(8)) multiplexer_1 (
    .in1(ACC_q), .in2(PC_q), .in4(STAT_q), .in7(MainMemoryRAM_dout), .out(multiplexer_1_out),
    .sel(decoder_1_out9));  // open: in0, in3, in5, in6
  Demultiplexer #(.select(3), .width(8)) demultiplexer_1 (
    .out0(demultiplexer_1_out0), .out1(demultiplexer_1_out1), .out2(demultiplexer_1_out2),
    .out3(demultiplexer_1_out3), .out4(demultiplexer_1_out4), .out5(demultiplexer_1_out5),
    .out6(demultiplexer_1_out6), .out7(demultiplexer_1_out7), .in(multiplexer_1_out), .sel(ProgramROM_data_2));
  RAM MainMemoryRAM (
    .addr(ACC_q), .we(decoder_1_out3), .oe(decoder_1_out2), .clk(decoder_1_out3), .din(rX_q),
    .dout(MainMemoryRAM_dout));
  Register r0 (.D(demultiplexer_1_out0), .en(decoder_1_out9[0]), .clk(decoder_1_out9[0]), .clr(Reset_out));  // open: Q
  Register r1 (.D(demultiplexer_1_out1), .en(decoder_1_out9[0]), .clk(decoder_1_out9[0]), .clr(Reset_out));  // open: Q
  Register r2 (.D(demultiplexer_1_out2), .en(decoder_1_out9[0]), .clk(decoder_1_out9[0]), .clr(Reset_out));  // open: Q
  Register r3 (.D(demultiplexer_1_out3), .en(decoder_1_out9[0]), .clk(decoder_1_out9[0]), .clr(Reset_out));  // open: Q
  Register r4 (.D(demultiplexer_1_out4), .en(decoder_1_out9[0]), .clk(decoder_1_out9[0]), .clr(Reset_out));  // open: Q
  Register r5 (.D(demultiplexer_1_out5), .en(decoder_1_out9[0]), .clk(decoder_1_out9[0]), .clr(Reset_out));  // open: Q
  Register r6 (.D(demultiplexer_1_out6), .en(decoder_1_out9[0]), .clk(decoder_1_out9[0]), .clr(Reset_out));  // open: Q
  Register r7 (.D(demultiplexer_1_out7), .en(decoder_1_out9[0]), .clk(decoder_1_out9[0]), .clr(Reset_out));  // open: Q

  // Notes on the sheet:
  //   HALT
  //   LD
  //   LI
  //   ST
  //   STPC
  //   STST
  //   STACC
  //   contents of ProgramROM (hex, n*v repeats v):
  //   f 10 e 18 49
endmodule
